# Fritzing sketch relay (saved by Fritzing 0.9.2b)
circuit board: 6.11987cm x 1.98764cm
breadboards: 1

parts:
  Relay = songle relay
  Q1 = NPN-Transistor [package="SOT-23 [SMD]"]
  D1 = Rectifier Diode [package="Melf DO-213 AA [SMD]"]
  optoIn_1k = Resistor [tolerance=±5% resistance=1k package="0805 [SMD]"]
  optoOut_220R = Resistor [tolerance=±5% resistance=220 package="0805 [SMD]"]
  Current = male pin header, 3 pins [form="♂ (male)"]
  Relay_Power = male pin header, 2 pins [form="♂ (male)"]
  MC_Unit = male pin header, 2 pins [form="♂ (male)"]
  U2 = Sharp PC817 [package=THT]

nets:
  N1: Relay.VCC, Q1.1, D1.anode
  N2: Relay.NO, Current.pin1
  N3: Relay.NC, Current.pin3
  N4: Relay.COMMON, Current.pin2
  N5: Relay.GND, D1.cathode, Relay_Power.pin2, U2.Pin_4
  N6: Q1.2, Relay_Power.pin1
  N7: Q1.0, optoOut_220R.Pin_0
  N8: optoIn_1k.Pin_0, U2.Pin_1
  N9: optoIn_1k.Pin_1, MC_Unit.pin2
  N10: optoOut_220R.Pin_1, U2.Pin_3
  N11: MC_Unit.pin1, U2.Pin_2
